// Logisim project Shift_reg.circ as structural Verilog: 1 circuit, main circuit main
module main (
  input  [11:0] Entrada,
  output Carry_Out,
  output [3:0] R,
  output [3:0] G,
  output [3:0] B
);

  wire clock_1_out, multiplexer_1_out;
  wire [3:0] counter_1_q;

  Clock clock_1 (.out(clock_1_out));
  Counter #(.width(4), .max('hf)) counter_1 (.Q(counter_1_q), .clk(clock_1_out));  // open: load, D, count, carry, clr
  Multiplexer #(.select(4)) multiplexer_1 (
    .in0(Entrada[11]), .in1(Entrada[10]), .in2(Entrada[9]), .in3(Entrada[8]), .in4(Entrada[7]),
    .in5(Entrada[6]), .in6(Entrada[5]), .in7(Entrada[4]), .in8(Entrada[3]), .in9(Entrada[2]),
    .in10(Entrada[1]), .in11(Entrada[0]), .out(multiplexer_1_out), .sel(counter_1_q));  // open: in12, in13, in14, in15, en
  D_Flip_Flop d_ff_1 (.clk(clock_1_out), .D(multiplexer_1_out), .Q(R[0]), .en(1'b1));  // open: Qn, preset, reset
  // Probe on R
  // Probe on G
  // Probe on B
  D_Flip_Flop d_ff_2 (.clk(clock_1_out), .D(R[0]), .Q(R[1]), .en(1'b1));  // open: Qn, preset, reset
  D_Flip_Flop d_ff_3 (.clk(clock_1_out), .D(R[1]), .Q(R[2]), .en(1'b1));  // open: Qn, preset, reset
  D_Flip_Flop d_ff_4 (.clk(clock_1_out), .D(R[2]), .Q(R[3]), .en(1'b1));  // open: Qn, preset, reset
  D_Flip_Flop d_ff_5 (.clk(clock_1_out), .D(R[3]), .Q(G[0]), .en(1'b1));  // open: Qn, preset, reset
  D_Flip_Flop d_ff_6 (.clk(clock_1_out), .D(G[0]), .Q(G[1]), .en(1'b1));  // open: Qn, preset, reset
  D_Flip_Flop d_ff_7 (.clk(clock_1_out), .D(G[1]), .Q(G[2]), .en(1'b1));  // open: Qn, preset, reset
  D_Flip_Flop d_ff_8 (.clk(clock_1_out), .D(G[2]), .Q(G[3]), .en(1'b1));  // open: Qn, preset, reset
  D_Flip_Flop d_ff_9 (.clk(clock_1_out), .D(G[3]), .Q(B[0]), .en(1'b1));  // open: Qn, preset, reset
  D_Flip_Flop d_ff_10 (.clk(clock_1_out), .D(B[0]), .Q(B[1]), .en(1'b1));  // open: Qn, preset, reset
  D_Flip_Flop d_ff_11 (.clk(clock_1_out), .D(B[1]), .Q(B[2]), .en(1'b1));  // open: Qn, preset, reset
  D_Flip_Flop d_ff_12 (.clk(clock_1_out), .D(B[2]), .Q(B[3]), .en(1'b1));  // open: Qn, preset, reset

  assign Carry_Out = B[3];

  // Notes on the sheet:
  //   CLK
  //   Data
endmodule
